# Fritzing sketch Wiring (saved by Fritzing 0.9.3b)
breadboards: 1

parts:
  元件1 = Arduino Uno (Rev3)
  DHT1 = DHT11_Temperature_and_Humitidy_Sensor
  元件2 = adafruit [part_number="Adafruit #2088"]
  OMRON1 = OMRON PCB Power Relay – G5LE [part_number="G5LE-1\n" package=THT]
  J1 = Piezo Speaker
  S1 = Round Pushbutton
  S2 = Round Pushbutton

nets:
  N1: 元件1.A0, 元件2.connector1
  N2: 元件1.A1, 元件2.connector3
  N3: 元件1.A2, 元件2.connector5
  N4: 元件1.A4/SDA, 元件2.connector7
  N5: 元件1.A5/SCL, 元件2.connector6
  N6: 元件1.D13/SCK, J1.pin2
  N7: 元件1.GND, DHT1.connector4, 元件2.connector2, OMRON1.COIL1, J1.pin1
  N8: 元件1.D4, DHT1.connector2
  N9: 元件1.D5_PWM, OMRON1.COIL2
  N10: 元件1.D6_PWM, S1.leg1
  N11: 元件1.D7, S2.leg1
  N12: 元件1.3V3, DHT1.connector1, S1.leg0, S2.leg0
  N13: 元件1.5V, 元件2.connector0
