# Fritzing sketch Wiring (saved by Fritzing 0.9.3b)

parts:
  U1 = ESP8266 WiFi Module [part_number=ESP8266]
  元件1 = Arduino Uno (Rev3)
  DHT1 = DHT11 Humitidy and Temperature Sensor

nets:
  N1: U1.RXD, 元件1.D4
  VCC: U1.VCC, U1.CH_PD, 元件1.3V3
  GND: U1.GND, 元件1.GND, DHT1.GND
  N2: U1.TXD, 元件1.D3_PWM
  N3: 元件1.D2, DHT1.DATA
  5V: 元件1.5V, DHT1.VDD

custom parts:
  DHT11 Humitidy and Temperature Sensor: DHT11 Humidity and Temperature Sensor
